// Logisim project e2310027.circ as structural Verilog: 1 circuit, main circuit main
module main (
  input  A1,
  input  A0,
  input  B1,
  input  B0,
  output X,
  output Y
);

  wire and_1_out, and_2_out, and_3_out, and_4_out, not_1_out, not_2_out, not_3_out, not_4_out, or_1_out,
       or_2_out, or_3_out, or_4_out;

  not not_1 (not_1_out, B1);
  not not_2 (not_2_out, B0);
  and and_1 (and_1_out, A1, not_1_out);
  or or_1 (or_1_out, A0, not_2_out);
  and and_2 (and_2_out, and_1_out, or_1_out);
  or or_2 (or_2_out, A1, not_1_out);
  and and_3 (and_3_out, A0, not_2_out);
  and and_4 (and_4_out, and_3_out, or_2_out);
  or or_3 (or_3_out, and_1_out, or_1_out);
  not not_3 (not_3_out, or_4_out);
  or or_4 (or_4_out, or_2_out, and_3_out);
  not not_4 (not_4_out, or_3_out);
  or or_5 (Y, and_4_out, not_4_out);
  or or_6 (X, and_2_out, not_3_out);
endmodule
